# Fritzing sketch rusl_1_2_sch (saved by Fritzing 0.9.3b)

parts:
  Часть1 = Arduino Nano (Rev3.0)
  M1 = RioRand LM2596
  ENC28J1 = ENC28J60

nets:
  N1: Часть1.D10, ENC28J1.CS
  N2: Часть1.D11/MOSI, ENC28J1.WOL
  N3: Часть1.D12/MISO, Часть1.D13/SCK, ENC28J1.SCK, ENC28J1.RST
  N4: Часть1.GND, M1.Pin_1
  N5: Часть1.5V, M1.Pin_2
  N6: M1.Pin_3, ENC28J1.VCC
  N7: M1.Pin_4, ENC28J1.GND

notes:
  распиновка ENC28J60
  отличается!
  ориентируйся по
  порядку пинов

custom parts:
  ENC28J60: Ethernet Module ENC28J60
